# Fritzing sketch fingerprint-schematic-design (saved by Fritzing 0.9.3b)

parts:
  Part1 = Arduino Uno (Rev3) - ICSP
  J1 = Piezo Speaker
  S1 = Pushbutton [package="[SMD]"]
  S2 = Pushbutton [package="[SMD]"]
  S3 = Pushbutton [package="[SMD]"]
  S4 = Pushbutton [package="[SMD]"]
  S5 = Pushbutton [package="[SMD]"]
  S6 = Pushbutton [package="[SMD]"]
  S7 = Pushbutton [package="[SMD]"]
  S8 = Pushbutton [package="[SMD]"]
  S9 = Pushbutton [package="[SMD]"]
  Part2 = sensor_biometrico
  Part3 = Arduino Uno (Rev3) - ICSP
  microSD1 = MicroSD Card Module
  Part4 = LCD1602-I2C

nets:
  N1: Part1.A0, S7.Pin_3, S7.Pin_4
  N2: Part1.A1, S8.Pin_3, S8.Pin_4
  N3: Part1.A2, S6.Pin_3, S6.Pin_4
  N4: Part1.A3, S9.Pin_3, S9.Pin_4
  N5: Part1.ICSP_MOSI, Part1.D11_PWM/MOSI, S5.Pin_1, S5.Pin_2
  N6: Part1.D8, S2.Pin_1, S2.Pin_2
  N7: Part1.D9_PWM, S3.Pin_1, S3.Pin_2
  N8: Part1.D10_PWM/SS, S4.Pin_1, S4.Pin_2
  GND: Part1.GND, J1.pin1, S1.Pin_3, S1.Pin_4, S2.Pin_3, S2.Pin_4, S3.Pin_3, S3.Pin_4, S4.Pin_3, S4.Pin_4, S5.Pin_3, S5.Pin_4, S6.Pin_1, S6.Pin_2, S7.Pin_1, S8.Pin_1, S9.Pin_1, S9.Pin_2, Part2.GND
  N9: Part1.D0/RX, Part3.D1/TX
  N10: Part1.D1/TX, Part3.D0/RX
  N11: Part1.D2, Part2.TX
  N12: Part1.D3_PWM, Part2.RX
  N13: Part1.D5_PWM, J1.pin2
  N14: Part1.D7, S1.Pin_1, S1.Pin_2
  5V: Part1.5V, Part2.VCC
  N15: Part3.A4/SDA, Part4.SDA
  N16: Part3.A5/SCL, Part4.SCL
  N17: Part3.ICSP_MOSI, Part3.D11_PWM/MOSI, microSD1.MOSI
  N18: Part3.D12/MISO, microSD1.MISO
  N19: Part3.D13/SCK, microSD1.SCK
  N20: Part3.D4, microSD1.CS
  VCC: Part3.5V, microSD1.VCC, Part4.VCC
  GND_2: Part3.GND, microSD1.GND, Part4.GND

notes:
  SLAVE
  SCHEMATIC
  MASTER SCHEMATIC

custom parts:
  sensor_biometrico: Adafruit Optical Fingerprint Sensor
  LCD1602-I2C: A standard character display, usually with 2x16 characters. Comes in many colors with LCM1602 IIC attached.
